# Fritzing sketch sketch (saved by Fritzing 0.9.2b)

parts:
  keyboard_board = Digispark
  receiver_board = Digispark
  IR_receiver = TSOP312.., 314.. [package=THT]
  part = Resistor [tolerance=±5% resistance=330 package=THT]
  indicator_LED = LED - 3mm [color="Blue (525nm)" package="3 mm [THT]"]
  li-ion_3_7v = LIPO-2000mAh [package=lipo-2000]
  bettery_charger_unit = TP4056 [chip_label=TP4056 package="DIP (Dual Inline) [THT]"]
  part_2 = Basic FET P-Channel [package="TO220 [THT]"]
  step_up_converter_(set_to_5V) = IC, DIP package, 4 pins
  part_3 = Rectifier Diode [part_number=1N4001 package="300 mil [THT]"]
  part_4 = Resistor [tolerance=±5% resistance=100k package=THT]
  sender_board = Digispark
  indicator_LED_2 = LED - 3mm [color="Blue (525nm)" package="3 mm [THT]"]
  IR_diode = LED - 3mm [color="Infrared (940nm)" package="3 mm [THT]"]
  send_button = Pushbutton [package="[THT]"]
  part_5 = Resistor [tolerance=±5% resistance=330 package=THT]
  part_6 = Resistor [tolerance=±5% resistance=51 package=THT]
  part_7 = Resistor [tolerance=±5% resistance=10k package=THT]

nets:
  VCC: keyboard_board.VCC, receiver_board.VCC, IR_receiver.Vs
  GND: keyboard_board.GND, receiver_board.GND, IR_receiver.GND, part.Pin_1
  N1: keyboard_board.P0, indicator_LED.anode
  N2: keyboard_board.P1, receiver_board.P1
  N3: keyboard_board.P2, receiver_board.P2
  N4: receiver_board.P0, IR_receiver.Data
  N5: part.Pin_0, indicator_LED.cathode
  N6: li-ion_3_7v.+, bettery_charger_unit.pin4
  N7: li-ion_3_7v.-, bettery_charger_unit.pin5
  N8: bettery_charger_unit.pin1, part_2.gate, part_3.anode, part_4.Pin_0
  N9: bettery_charger_unit.pin3, part_2.drain
  N10: bettery_charger_unit.pin6, step_up_converter_(set_to_5V).pin4, part_4.Pin_1
  N11: part_2.source, step_up_converter_(set_to_5V).pin3, part_3.cathode
  N12: step_up_converter_(set_to_5V).pin1, sender_board.GND, part_5.Pin_0, part_6.Pin_0, part_7.Pin_0
  N13: step_up_converter_(set_to_5V).pin2, sender_board.VCC
  N14: sender_board.P0, indicator_LED_2.anode
  N15: sender_board.P1, IR_diode.anode
  N16: sender_board.P2, send_button.Pin_1
  N17: indicator_LED_2.cathode, part_5.Pin_1
  N18: IR_diode.cathode, part_6.Pin_1
  N19: send_button.Pin_3, send_button.Pin_4, part_7.Pin_1

custom parts:
  Digispark: The Digispark is an Attiny85 based microcontroller development board similar to the Arduino line, only cheaper, smaller, and a bit less powerful. With a whole host of shields to extend its functionality and the ability to use the familiar Arduino IDE the Digispark is a great way to jump into electronics, or perfect for when an Arduino is too big or too much.
  TP4056: A DIP stand-in part for whatever IC you want. With 6 pins on a 300mil dual inline package (DIP) footprint.
